# Fritzing sketch Sketch (saved by Fritzing 0.9.3b)
breadboards: 1

parts:
  HELTEC_-_LORA = Heltec WiFi Kit 8 [part_number=HTIT-W8266]
  DS1 = DS18B20 1-Wire Temperature Sensor [part_number=DS18B20]
  Condutivimetro = Soil Moisture Sensor
  R1 = Resistor [tolerance=±5% resistance=4.7k package="0805 [SMD]"]

nets:
  N1: HELTEC_-_LORA.pin_6, Condutivimetro.SIG
  GND: HELTEC_-_LORA.pin_9, HELTEC_-_LORA.pin_12, HELTEC_-_LORA.pin_16, DS1.GND, Condutivimetro.GND
  VDD: HELTEC_-_LORA.pin_11, HELTEC_-_LORA.pin_14, DS1.VDD, Condutivimetro.VCC, R1.Pin_0
  N2: HELTEC_-_LORA.pin_21, DS1.DQ, R1.Pin_1

custom parts:
  Heltec WiFi Kit 8: The Heltec WiFi Kit 8 is an IoT development board designed and produced by Heltec Automation and based on the Espressif ESP8266 processor module. The board includes built-in WiFi, a 0.91″ OLED display and a Li-Po battery management system. Links: Heltec WiFi Kit 8 product page Github
